# Fritzing sketch circuit (saved by Fritzing 0.9.3b)

parts:
  Part2 = Arduino Pro Mini V2 (5V)
  RCWL-0516_Microwave_Radar_Motion_Sensor1 = RCWL-0516 Microwave Radar Motion Sensor Module
  Part3 = Adafruit MAX9814 Electret Microphone Amplifier [part_number="Adafruit #1713"]
  J1 = Piezo Speaker
  R2 = Resistor [tolerance=±5% resistance=220 package="0805 [SMD]"]
  J2 = Dagu DGServo 9g header (male) [package=THT]
  R1 = Resistor [tolerance=±5% resistance=220 package="0805 [SMD]"]
  Part4 = Adafruit AT42QT1010 Standalone Momentary Capacitive Touch Sensor [part_number="Adafruit #1374"]
  Part5 = Adafruit APDS-9960 [part_number="Adafruit #3595"]

nets:
  GND: Part2.GND, RCWL-0516_Microwave_Radar_Motion_Sensor1.GND, Part3.GND, J1.pin1, J2.gnd, Part4.GND, Part5.GND
  N1: Part2.A4, Part5.SDA
  N2: Part2.A5, Part5.SCL
  VCC: Part2.VCC, RCWL-0516_Microwave_Radar_Motion_Sensor1.VIN, Part3.VDD, J2.Vcc, Part4.VDD, Part5.VIN
  N3: Part2.A0, Part3.OUTPUT
  N4: Part2.MOSI, R2.Pin_0
  N5: Part2.D10, R1.Pin_0
  N6: Part2.D9, Part4.OUT
  N7: Part2.D2, RCWL-0516_Microwave_Radar_Motion_Sensor1.OUT
  N8: J1.pin2, R2.Pin_1
  N9: J2.pulse, R1.Pin_1

custom parts:
  Arduino Pro Mini V2 (5V): Arduino Pro Mini V2 There are several different layouts for this board out there. This one is modeled after the Sparkfun 11113 board but a few of the pins have been moved around.
  RCWL-0516 Microwave Radar Motion Sensor Module: The RCWL-0516 is a microwave radar motion sensor module. Input voltage is 4V to 28V. The 3V3 pin is a power output.
  Adafruit MAX9814 Electret Microphone Amplifier: Add an ear to your project with this well-designed electret microphone amplifier with AGC. This fully assembled and tested board comes with a 20-20KHz electret microphone soldered on. For the amplification, we use the Maxim MAX9814, a specialty chip that is designed for amplifying electret microphones in situations where the loudness of the audio isn't predictable. This fancy microphone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
  Adafruit AT42QT1010 Standalone Momentary Capacitive Touch Sensor: This breakout board is the simplest way to create a project with a single "momentary" capacitive touch sensor. No microcontroller is required here - just power with 1.8 to 5.5VDC and touch the pad to activate the sensor. When a capacitive load is detected (e.g. a person touches the sensor-pad area) the red LED lights up and the output pin goes high. You can also solder a wire to the middle pad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
  Adafruit APDS-9960: The APDS9960 from Avago Technologies has an integrated IR LED and driver, along with four directional photodiodes that sense reflected IR energy from the LED. It's proximity detection feature allows it to measure the distance an object is from the front of the sensor (up to a few centimeters) with 8 bit resolution. Since there are four IR sensors, you can measure the changes in light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
